// Logisim project Adder Concatenation.circ as structural Verilog: 3 circuits, main circuit Main
module _4BitAdder (
  input  [3:0] in_1,
  input  [3:0] in_2,
  input  in_3,
  output out_4,
  output [3:0] out_5
);

  wire full_adder_2_out_4, full_adder_3_out_4, full_adder_4_out_4;

  Full_Adder full_adder_1 (.in_1(in_1[3]), .in_2(in_2[3]), .in_3(full_adder_2_out_4), .out_4(out_4), .out_5(out_5[3]));
  Full_Adder full_adder_2 (
    .in_1(in_1[2]), .in_2(in_2[2]), .in_3(full_adder_3_out_4), .out_4(full_adder_2_out_4), .out_5(out_5[2]));
  Full_Adder full_adder_3 (
    .in_1(in_1[1]), .in_2(in_2[1]), .in_3(full_adder_4_out_4), .out_4(full_adder_3_out_4), .out_5(out_5[1]));
  Full_Adder full_adder_4 (.in_1(in_1[0]), .in_2(in_2[0]), .in_3(in_3), .out_4(full_adder_4_out_4), .out_5(out_5[0]));
endmodule

module Full_Adder (
  input  in_1,
  input  in_2,
  input  in_3,
  output out_4,
  output out_5
);

  wire or_1_out, xnor_1_out;

  NotExactlyOne xnor_1 (.out(xnor_1_out), .in0(in_1), .in1(in_2), .in2(in_3));
  or or_1 (or_1_out, in_1, in_2, in_3);
  xor xor_1 (out_5, in_1, in_2, in_3);
  and and_1 (out_4, xnor_1_out, or_1_out);
endmodule

module Main (
  input  [7:0] in_1,
  input  [7:0] in_2,
  input  in_3,
  output out_4,
  output [7:0] out_5
);

  wire n4bitadder_2_out_4;

  _4BitAdder u_4bitadder_1 (
    .in_1(in_1[7:4]), .in_2(in_2[7:4]), .out_4(out_4), .out_5(out_5[7:4]), .in_3(n4bitadder_2_out_4));
  _4BitAdder u_4bitadder_2 (
    .in_1(in_1[3:0]), .in_2(in_2[3:0]), .out_4(n4bitadder_2_out_4), .out_5(out_5[3:0]), .in_3(in_3));
endmodule
