// Logisim project Full Adder.circ as structural Verilog: 2 circuits, main circuit main
module main (
  input  in_1,
  input  in_2,
  input  in_3,
  input  in_4,
  input  in_5,
  input  in_6,
  input  in_7,
  input  in_8,
  output out_9,
  output out_10,
  output out_11,
  output out_12,
  output out_13
);

  wire full_adder_2_out_4, full_adder_3_out_4, full_adder_4_out_4;

  Full_Adder full_adder_1 (.in_1(in_1), .in_2(in_5), .in_3(full_adder_2_out_4), .out_4(out_9), .out_5(out_10));
  Full_Adder full_adder_2 (
    .in_1(in_2), .in_2(in_6), .in_3(full_adder_3_out_4), .out_4(full_adder_2_out_4), .out_5(out_11));
  Full_Adder full_adder_3 (
    .in_1(in_3), .in_2(in_7), .in_3(full_adder_4_out_4), .out_4(full_adder_3_out_4), .out_5(out_12));
  Full_Adder full_adder_4 (.in_1(in_4), .in_2(in_8), .in_3(1'b0), .out_4(full_adder_4_out_4), .out_5(out_13));
endmodule

module Full_Adder (
  input  in_1,
  input  in_2,
  input  in_3,
  output out_4,
  output out_5
);

  wire or_1_out, xnor_1_out;

  NotExactlyOne xnor_1 (.out(xnor_1_out), .in0(in_1), .in1(in_2), .in2(in_3));
  or or_1 (or_1_out, in_1, in_2, in_3);
  and and_1 (out_4, xnor_1_out, or_1_out);
  xor xor_1 (out_5, in_1, in_2, in_3);
endmodule
