// Logisim project SimpleALU.circ as structural Verilog: 4 circuits, main circuit Main
module _8BitALU (
  input  add,
  input  \and ,
  input  \or ,
  input  \xor ,
  input  left_shift,
  input  right_shift,
  input  sub,
  input  [7:0] rhs,
  input  [7:0] lhs,
  output [7:0] \output ,
  output carry_out
);

  wire or_2_out;
  wire [7:0] adder_1_out, and_1_out, bit_extender_1_out, or_1_out, shiftleft_1_out_2, shiftright_1_out_2,
       xor_1_out, xor_2_out;

  assign bit_extender_1_out = {{7{sub}}, sub};  // Bit_Extender bit_extender_1
  assign xor_1_out = bit_extender_1_out ^ rhs;  // XOR_Gate xor_1, 8 bits wide
  assign and_1_out = rhs & lhs;  // AND_Gate and_1, 8 bits wide
  assign or_1_out = rhs | lhs;  // OR_Gate or_1, 8 bits wide
  assign xor_2_out = rhs ^ lhs;  // XOR_Gate xor_2, 8 bits wide
  ShiftLeft shiftleft_1 (.in_1(lhs), .out_2(shiftleft_1_out_2));
  ShiftRight shiftright_1 (.in_1(lhs), .out_2(shiftright_1_out_2));
  Adder adder_1 (.a(xor_1_out), .b(lhs), .out(adder_1_out), .cin(sub), .cout(carry_out));
  or or_2 (or_2_out, add, sub);
  assign \output  = or_2_out ? adder_1_out : 8'bz;  // Controlled_Buffer controlled_buffer_1
  assign \output  = \and  ? and_1_out : 8'bz;  // Controlled_Buffer controlled_buffer_2
  assign \output  = \or  ? or_1_out : 8'bz;  // Controlled_Buffer controlled_buffer_3
  assign \output  = \xor  ? xor_2_out : 8'bz;  // Controlled_Buffer controlled_buffer_4
  assign \output  = left_shift ? shiftleft_1_out_2 : 8'bz;  // Controlled_Buffer controlled_buffer_5
  assign \output  = right_shift ? shiftright_1_out_2 : 8'bz;  // Controlled_Buffer controlled_buffer_6
endmodule

module ShiftLeft (
  input  [7:0] in_1,
  output [7:0] out_2
);


  assign out_2 = {in_1[6:0], 1'b0};
endmodule

module ShiftRight (
  input  [7:0] in_1,
  output [7:0] out_2
);


  assign out_2 = {1'b0, in_1[7:1]};
endmodule

module Main (
  input  [7:0] bus,
  input  in_2,
  input  in_3,
  input  in_4,
  input  in_5,
  input  in_6,
  input  in_7,
  input  in_8,
  input  in_9,
  input  in_10,
  input  enable_lhs,
  input  enable_rhs,
  input  clock,
  input  _0,
  input  in_15,
  input  in_16,
  input  in_17,
  input  in_18,
  output out_19
);

  wire [7:0] controlled_buffer_1_out, controlled_buffer_2_out, n8bitalu_1_output, register_1_q, register_2_q;

  assign controlled_buffer_1_out = in_2 ? bus : 8'bz;  // Controlled_Buffer controlled_buffer_1
  assign controlled_buffer_2_out = in_10 ? {8{1'b0}} : 8'bz;  // Controlled_Buffer controlled_buffer_2
  assign controlled_buffer_1_out = in_17 ? register_2_q : 8'bz;  // Controlled_Buffer controlled_buffer_3
  assign controlled_buffer_1_out = in_15 ? register_1_q : 8'bz;  // Controlled_Buffer controlled_buffer_4
  assign controlled_buffer_2_out = in_16 ? register_1_q : 8'bz;  // Controlled_Buffer controlled_buffer_5
  Register register_1 (.D(n8bitalu_1_output), .en(enable_lhs), .Q(register_1_q), .clk(clock), .clr(_0));
  Register register_2 (.D(n8bitalu_1_output), .en(enable_rhs), .Q(register_2_q), .clk(clock), .clr(_0));
  assign controlled_buffer_2_out = in_18 ? register_2_q : 8'bz;  // Controlled_Buffer controlled_buffer_6
  _8BitALU u_8bitalu_1 (
    .add(in_3), .\and (in_5), .\or (in_6), .\xor (in_7), .left_shift(in_8), .right_shift(in_9), .sub(in_4),
    .\output (n8bitalu_1_output), .carry_out(out_19), .lhs(controlled_buffer_1_out),
    .rhs(controlled_buffer_2_out));
endmodule
