// Logisim project Subtractor.circ as structural Verilog: 2 circuits, main circuit main
module main (
  input  in_1,
  input  in_2,
  input  in_3,
  input  in_4,
  input  in_5,
  input  in_6,
  input  in_7,
  input  in_8,
  input  in_9,
  output out_10,
  output out_11,
  output out_12,
  output out_13,
  output out_14
);

  wire full_adder_2_out_4, full_adder_3_out_4, full_adder_4_out_4, xor_1_out, xor_2_out, xor_3_out, xor_4_out;

  xor xor_1 (xor_1_out, in_5, in_9);
  xor xor_2 (xor_2_out, in_6, in_9);
  xor xor_3 (xor_3_out, in_7, in_9);
  xor xor_4 (xor_4_out, in_8, in_9);
  Full_Adder full_adder_1 (.in_1(in_1), .in_2(xor_1_out), .in_3(full_adder_2_out_4), .out_4(out_10), .out_5(out_11));
  Full_Adder full_adder_2 (
    .in_1(in_2), .in_2(xor_2_out), .in_3(full_adder_3_out_4), .out_4(full_adder_2_out_4), .out_5(out_12));
  Full_Adder full_adder_3 (
    .in_1(in_3), .in_2(xor_3_out), .in_3(full_adder_4_out_4), .out_4(full_adder_3_out_4), .out_5(out_13));
  Full_Adder full_adder_4 (.in_1(in_4), .in_2(xor_4_out), .in_3(in_9), .out_4(full_adder_4_out_4), .out_5(out_14));
endmodule

module Full_Adder (
  input  in_1,
  input  in_2,
  input  in_3,
  output out_4,
  output out_5
);

  wire or_1_out, xnor_1_out;

  NotExactlyOne xnor_1 (.out(xnor_1_out), .in0(in_1), .in1(in_2), .in2(in_3));
  or or_1 (or_1_out, in_1, in_2, in_3);
  xor xor_1 (out_5, in_1, in_2, in_3);
  and and_1 (out_4, xnor_1_out, or_1_out);
endmodule
