// Logisim project CPU.circ as structural Verilog: 4 circuits, main circuit Main
module _8BitALU (
  input  add,
  input  \and ,
  input  \or ,
  input  \xor ,
  input  left_shift,
  input  right_shift,
  input  sub,
  input  [7:0] rhs,
  input  [7:0] lhs,
  output [7:0] \output ,
  output carry_out,
  output _0,
  output sign
);

  wire adder_1_cout, or_2_out, shiftleft_1_out_3, shiftright_1_out_2;
  wire [7:0] adder_1_out, and_1_out, bit_extender_1_out, or_1_out, shiftleft_1_out_2, shiftright_1_out_3,
       xor_1_out, xor_2_out;

  assign bit_extender_1_out = {{7{sub}}, sub};  // Bit_Extender bit_extender_1
  assign xor_1_out = bit_extender_1_out ^ rhs;  // XOR_Gate xor_1, 8 bits wide
  assign carry_out = or_2_out ? adder_1_cout : 1'bz;  // Controlled_Buffer controlled_buffer_1
  assign and_1_out = rhs & lhs;  // AND_Gate and_1, 8 bits wide
  assign or_1_out = rhs | lhs;  // OR_Gate or_1, 8 bits wide
  assign xor_2_out = rhs ^ lhs;  // XOR_Gate xor_2, 8 bits wide
  ShiftLeft shiftleft_1 (.in_1(lhs), .out_2(shiftleft_1_out_2), .out_3(shiftleft_1_out_3));
  ShiftRight shiftright_1 (.in_1(lhs), .out_3(shiftright_1_out_3), .out_2(shiftright_1_out_2));
  Adder adder_1 (.a(xor_1_out), .b(lhs), .out(adder_1_out), .cin(sub), .cout(adder_1_cout));
  assign carry_out = left_shift ? shiftleft_1_out_3 : 1'bz;  // Controlled_Buffer controlled_buffer_2
  assign carry_out = right_shift ? shiftright_1_out_2 : 1'bz;  // Controlled_Buffer controlled_buffer_3
  or or_2 (or_2_out, add, sub);
  assign \output  = or_2_out ? adder_1_out : 8'bz;  // Controlled_Buffer controlled_buffer_4
  assign \output  = \and  ? and_1_out : 8'bz;  // Controlled_Buffer controlled_buffer_5
  assign \output  = \or  ? or_1_out : 8'bz;  // Controlled_Buffer controlled_buffer_6
  assign \output  = \xor  ? xor_2_out : 8'bz;  // Controlled_Buffer controlled_buffer_7
  assign \output  = left_shift ? shiftleft_1_out_2 : 8'bz;  // Controlled_Buffer controlled_buffer_8
  assign \output  = right_shift ? shiftright_1_out_3 : 8'bz;  // Controlled_Buffer controlled_buffer_9
  nor nor_1 (_0, \output [0], \output [1], \output [2], \output [3], \output [5], \output [6], \output [7], \output [4]);

  assign sign = \output [7];
endmodule

module ShiftLeft (
  input  [7:0] in_1,
  output [7:0] out_2,
  output out_3
);


  assign out_2 = {in_1[6:0], 1'b0};
  assign out_3 = in_1[7];
endmodule

module ShiftRight (
  input  [7:0] in_1,
  output out_2,
  output [7:0] out_3
);


  assign out_2 = in_1[0];
  assign out_3 = {1'b0, in_1[7:1]};
endmodule

module Main (
  input  reset
);

  wire and_1_out, and_2_out, and_3_out, clock_out, controlled_buffer_2_out, d_ff_1_q, d_ff_5_q,
       decoder_1_out0, decoder_1_out1, decoder_1_out2, decoder_1_out3, decoder_1_out4, decoder_1_out5,
       decoder_1_out6, n8bitalu_1__0, n8bitalu_1_carry_out, n8bitalu_1_sign;
  wire [5:0] not_1_out;
  wire [7:0] controlled_buffer_3_out, counter_1_q, multiplexer_1_out, multiplexer_2_out, multiplexer_3_out,
       n8bitalu_1_output, register_1_q, register_2_q;
  wire [7:2] multiplexer_4_out;
  wire [20:0] controlled_buffer_1_out;

  Clock clock (.out(clock_out));
  Register register_1 (
    .D(n8bitalu_1_output), .en(controlled_buffer_1_out[0]), .Q(register_1_q), .clk(clock_out), .clr(reset));
  Register register_2 (
    .D(n8bitalu_1_output), .en(controlled_buffer_1_out[1]), .Q(register_2_q), .clk(clock_out), .clr(reset));
  D_Flip_Flop d_ff_1 (
    .clk(clock_out), .D(controlled_buffer_2_out), .Q(d_ff_1_q), .preset(reset));  // open: Qn, en, reset
  and and_1 (and_1_out, d_ff_1_q, and_3_out);
  Multiplexer #(.select(3), .width(8), .enable("false")) multiplexer_1 (
    .in0(register_1_q), .in1(register_2_q), .in2(controlled_buffer_3_out), .out(multiplexer_1_out),
    .sel(controlled_buffer_1_out[7:5]));  // open: in3, in4, in5, in6, in7
  Multiplexer #(.select(3), .width(8), .enable("false")) multiplexer_2 (
    .in0(register_1_q), .in1(register_2_q), .in2({8{1'b0}}), .out(multiplexer_2_out),
    .sel(controlled_buffer_1_out[4:2]));  // open: in3, in4, in5, in6, in7
  not not_1 (not_1_out[0], not_1_out[1]);
  assign controlled_buffer_1_out = and_1_out ? {15'h5404, not_1_out[5], 3'b010, not_1_out[1:0]} : 21'bz;  // Controlled_Buffer controlled_buffer_1
  Counter counter_1 (
    .load(controlled_buffer_1_out[15]), .D(n8bitalu_1_output), .count(controlled_buffer_1_out[16]),
    .Q(counter_1_q), .clk(clock_out), .clr(reset));  // open: carry
  assign controlled_buffer_2_out = and_1_out ? 1'b1 : 1'bz;  // Controlled_Buffer controlled_buffer_2
  Decoder #(.select(3), .enable("false")) decoder_1 (
    .out0(decoder_1_out0), .out1(decoder_1_out1), .out2(decoder_1_out2), .out3(decoder_1_out3),
    .out4(decoder_1_out4), .out5(decoder_1_out5), .out6(decoder_1_out6), .sel(controlled_buffer_1_out[10:8]));  // open: out7
  Multiplexer #(.select(3), .width(8), .enable("false")) multiplexer_3 (
    .in0(multiplexer_1_out), .in1(multiplexer_2_out), .in2(counter_1_q), .out(multiplexer_3_out),
    .sel(controlled_buffer_1_out[19:17]));  // open: in3, in4, in5, in6, in7
  _8BitALU u_8bitalu_1 (
    .add(decoder_1_out0), .\and (decoder_1_out2), .\or (decoder_1_out3), .\xor (decoder_1_out4),
    .left_shift(decoder_1_out5), .right_shift(decoder_1_out6), .sub(decoder_1_out1),
    .\output (n8bitalu_1_output), .carry_out(n8bitalu_1_carry_out), .lhs(multiplexer_1_out),
    .rhs(multiplexer_2_out), ._0(n8bitalu_1__0), .sign(n8bitalu_1_sign));
  D_Flip_Flop d_ff_2 (
    .clk(clock_out), .D(n8bitalu_1_carry_out), .en(controlled_buffer_1_out[11]), .reset(reset));  // open: Q, Qn, preset
  D_Flip_Flop d_ff_3 (
    .clk(clock_out), .D(n8bitalu_1__0), .en(controlled_buffer_1_out[12]), .reset(reset));  // open: Q, Qn, preset
  D_Flip_Flop d_ff_4 (
    .clk(clock_out), .D(n8bitalu_1_sign), .en(controlled_buffer_1_out[13]), .reset(reset));  // open: Q, Qn, preset
  and and_2 (and_2_out, d_ff_1_q, ~controlled_buffer_2_out);  // AND_Gate
  assign controlled_buffer_3_out = controlled_buffer_1_out[14] ? n8bitalu_1_output : 8'bz;  // Controlled_Buffer controlled_buffer_3
  RAM ram_1 (
    .addr(multiplexer_3_out), .data(controlled_buffer_3_out), .sel(1'b1), .clk(clock_out),
    .ld(controlled_buffer_1_out[20]));  // open: clr
  Multiplexer #(.width(8), .enable("false")) multiplexer_4 (
    .in0(controlled_buffer_3_out), .in1({8{1'b0}}), .out({multiplexer_4_out, not_1_out[1], not_1_out[5]}),
    .sel(reset));
  D_Flip_Flop d_ff_5 (.clk(clock_out), .D(and_2_out), .Q(d_ff_5_q), .reset(reset));  // open: Qn, preset, en
  and and_3 (and_3_out, ~multiplexer_4_out[4], ~multiplexer_4_out[5], ~multiplexer_4_out[7], ~multiplexer_4_out[6]);  // AND_Gate

  // Notes on the sheet:
  //   ip
  //   ALU
  //   mov
endmodule
