// Logisim project 8BitRegister.circ as structural Verilog
module ETFF (
  input  data,
  input  clock,
  input  _0,
  output out_4
);

  wire de_latch_1_out_4, not_1_out;

  DE_Latch de_latch_1 (.data(data), .enable(not_1_out), .set(_0), .out_4(de_latch_1_out_4));
  not not_1 (not_1_out, clock);
  DE_Latch de_latch_2 (.data(de_latch_1_out_4), .enable(clock), .set(_0), .out_4(out_4));

  // Notes on the sheet:
  //   edge-triggered de flip flop
endmodule

module SR_Latch (
  input  set,
  input  reset,
  output out_3
);

  wire nor_1_out;

  nor nor_1 (nor_1_out, set, out_3);
  nor nor_2 (out_3, nor_1_out, reset);
endmodule

module DE_Latch (
  input  data,
  input  enable,
  input  set,
  output out_4
);

  wire and_1_out, and_2_out, nor_1_out, not_1_out, or_1_out;

  not not_1 (not_1_out, data);
  and and_1 (and_1_out, data, enable);
  and and_2 (and_2_out, enable, not_1_out);
  or or_1 (or_1_out, and_2_out, set);
  nor nor_1 (nor_1_out, and_1_out, out_4);
  nor nor_2 (out_4, nor_1_out, or_1_out);
endmodule

module Register (
  input  [7:0] date,
  input  enable,
  input  clock,
  input  _0,
  output [7:0] \output 
);

  wire and_1_out;

  and and_1 (and_1_out, enable, clock);
  ETFF etff_1 (.data(date[0]), .clock(and_1_out), ._0(_0), .out_4(\output [0]));
  ETFF etff_2 (.data(date[4]), .clock(and_1_out), ._0(_0), .out_4(\output [4]));
  ETFF etff_3 (.data(date[1]), .clock(and_1_out), ._0(_0), .out_4(\output [1]));
  ETFF etff_4 (.data(date[5]), .clock(and_1_out), ._0(_0), .out_4(\output [5]));
  ETFF etff_5 (.data(date[2]), .clock(and_1_out), ._0(_0), .out_4(\output [2]));
  ETFF etff_6 (.data(date[6]), .clock(and_1_out), ._0(_0), .out_4(\output [6]));
  ETFF etff_7 (.data(date[3]), .clock(and_1_out), ._0(_0), .out_4(\output [3]));
  ETFF etff_8 (.data(date[7]), .clock(and_1_out), ._0(_0), .out_4(\output [7]));
endmodule
