// Logisim project Counter.circ as structural Verilog: 2 circuits, main circuit Counter
module _2BitCounter (
  input  clock,
  input  count,
  input  reset,
  output carry,
  output high,
  output low
);

  wire and_1_out;

  and and_1 (and_1_out, ~clock, low);  // AND_Gate
  and and_2 (carry, low, high, ~clock);  // AND_Gate
  T_Flip_Flop t_ff_1 (.clk(clock), .T(and_1_out), .Q(high), .reset(reset));  // open: Qn, preset, en
  T_Flip_Flop t_ff_2 (.clk(clock), .T(count), .Q(low), .reset(reset));  // open: Qn, preset, en
endmodule

module Counter (
  input  clock,
  input  count,
  input  _0,
  output [5:0] out_4
);

  wire and_1_out, and_2_out, n2bitcounter_2_carry, n2bitcounter_3_carry;

  and and_1 (and_1_out, n2bitcounter_2_carry, and_2_out, clock);
  _2BitCounter u_2bitcounter_1 (
    .clock(and_1_out), .count(count), .reset(_0), .high(out_4[5]), .low(out_4[4]));  // open: carry
  and and_2 (and_2_out, n2bitcounter_3_carry, clock);
  _2BitCounter u_2bitcounter_2 (
    .carry(n2bitcounter_2_carry), .clock(and_2_out), .count(count), .reset(_0), .high(out_4[3]),
    .low(out_4[2]));
  _2BitCounter u_2bitcounter_3 (
    .carry(n2bitcounter_3_carry), .clock(clock), .count(count), .reset(_0), .high(out_4[1]), .low(out_4[0]));
endmodule
