// Logisim project SimpleRAM.circ as structural Verilog: 1 circuit, main circuit main
module main (
  input  enable,
  input  [2:0] address,
  input  read_nwrite,
  input  clock,
  input  [7:0] in_5,
  input  data_in,
  output [7:0] out_7
);

  wire and_1_out, and_2_out, and_3_out, and_4_out, and_5_out, and_6_out, and_7_out, and_8_out, and_9_out,
       and_10_out, decoder_1_out3, decoder_1_out4, decoder_1_out5, decoder_1_out6, decoder_1_out7;
  wire [7:0] register_1_q, register_2_q, register_3_q, register_4_q, register_5_q;

  Decoder #(.select(3)) decoder_1 (
    .out3(decoder_1_out3), .out4(decoder_1_out4), .out5(decoder_1_out5), .out6(decoder_1_out6),
    .out7(decoder_1_out7), .sel(address), .en(enable));  // open: out0, out1, out2
  and and_1 (and_1_out, decoder_1_out3, ~read_nwrite);  // AND_Gate
  and and_2 (and_2_out, decoder_1_out4, ~read_nwrite);  // AND_Gate
  and and_3 (and_3_out, decoder_1_out5, ~read_nwrite);  // AND_Gate
  and and_4 (and_4_out, decoder_1_out6, ~read_nwrite);  // AND_Gate
  and and_5 (and_5_out, decoder_1_out7, ~read_nwrite);  // AND_Gate
  Register register_1 (.D(out_7), .en(and_1_out), .Q(register_1_q), .clk(clock));  // open: clr
  Register register_2 (.D(out_7), .en(and_2_out), .Q(register_2_q), .clk(clock));  // open: clr
  Register register_3 (.D(out_7), .en(and_3_out), .Q(register_3_q), .clk(clock));  // open: clr
  Register register_4 (.D(out_7), .en(and_4_out), .Q(register_4_q), .clk(clock));  // open: clr
  Register register_5 (.D(out_7), .en(and_5_out), .Q(register_5_q), .clk(clock));  // open: clr
  assign out_7 = and_6_out ? register_1_q : 8'bz;  // Controlled_Buffer controlled_buffer_1
  and and_6 (and_6_out, read_nwrite, decoder_1_out3);
  assign out_7 = and_7_out ? register_2_q : 8'bz;  // Controlled_Buffer controlled_buffer_2
  and and_7 (and_7_out, read_nwrite, decoder_1_out4);
  assign out_7 = and_8_out ? register_3_q : 8'bz;  // Controlled_Buffer controlled_buffer_3
  and and_8 (and_8_out, read_nwrite, decoder_1_out5);
  assign out_7 = and_9_out ? register_4_q : 8'bz;  // Controlled_Buffer controlled_buffer_4
  and and_9 (and_9_out, read_nwrite, decoder_1_out6);
  assign out_7 = and_10_out ? register_5_q : 8'bz;  // Controlled_Buffer controlled_buffer_5
  and and_10 (and_10_out, read_nwrite, decoder_1_out7);
  assign out_7 = data_in ? in_5 : 8'bz;  // Controlled_Buffer controlled_buffer_6
endmodule
