// Logisim project Decoder.circ as structural Verilog: 2 circuits, main circuit 4BitDecoder
module BinaryDecoder (
  input  [1:0] in_1,
  input  enable,
  output out_3,
  output out_4,
  output out_5,
  output out_6
);

  and and_1 (out_3, ~in_1[0], enable, ~in_1[1]);  // AND_Gate
  and and_2 (out_4, in_1[0], enable, ~in_1[1]);  // AND_Gate
  and and_3 (out_5, ~in_1[0], enable, in_1[1]);  // AND_Gate
  and and_4 (out_6, in_1[0], enable, in_1[1]);
endmodule

module _4BitDecoder (
  input  [3:0] in_1,
  input  enable
);

  wire binarydecoder_1_out_3, binarydecoder_1_out_4, binarydecoder_1_out_5, binarydecoder_1_out_6;

  BinaryDecoder binarydecoder_1 (
    .out_3(binarydecoder_1_out_3), .out_4(binarydecoder_1_out_4), .out_5(binarydecoder_1_out_5),
    .out_6(binarydecoder_1_out_6), .enable(enable), .in_1(in_1[3:2]));
  BinaryDecoder binarydecoder_2 (.enable(binarydecoder_1_out_3), .in_1(in_1[1:0]));  // open: out_3, out_4, out_5, out_6
  BinaryDecoder binarydecoder_3 (.enable(binarydecoder_1_out_4), .in_1(in_1[1:0]));  // open: out_3, out_4, out_5, out_6
  BinaryDecoder binarydecoder_4 (.enable(binarydecoder_1_out_5), .in_1(in_1[1:0]));  // open: out_3, out_4, out_5, out_6
  BinaryDecoder binarydecoder_5 (.enable(binarydecoder_1_out_6), .in_1(in_1[1:0]));  // open: out_3, out_4, out_5, out_6
endmodule
