// Logisim project 8BitRegister.circ as structural Verilog
module ETFF (
  input  in_1,
  input  in_2,
  input  in_3,
  output out_4
);

  wire de_latch_1_out_4, not_1_out;

  DE_Latch de_latch_1 (.data(in_1), .enable(in_2), .set(in_3), .out_4(de_latch_1_out_4));
  not not_1 (not_1_out, in_2);
  DE_Latch de_latch_2 (.data(de_latch_1_out_4), .enable(not_1_out), .set(in_3), .out_4(out_4));

  // Notes on the sheet:
  //   edge-triggered de flip flop
endmodule

module SR_Latch (
  input  set,
  input  reset,
  output out_3
);

  wire nor_1_out;

  nor nor_1 (nor_1_out, set, out_3);
  nor nor_2 (out_3, nor_1_out, reset);
endmodule

module DE_Latch (
  input  data,
  input  enable,
  input  set,
  output out_4
);

  wire and_1_out, and_2_out, nor_1_out, not_1_out, or_1_out;

  not not_1 (not_1_out, data);
  and and_1 (and_1_out, data, enable);
  and and_2 (and_2_out, enable, not_1_out);
  or or_1 (or_1_out, and_2_out, set);
  nor nor_1 (nor_1_out, and_1_out, out_4);
  nor nor_2 (out_4, nor_1_out, or_1_out);
endmodule

module Register (
  input  [7:0] date,
  input  enable,
  input  clock,
  input  _0,
  output [7:0] \output 
);

  wire and_1_out, not_1_out;

  and and_1 (and_1_out, enable, clock);
  ETFF etff_1 (.in_1(date[0]), .in_2(not_1_out), .in_3(_0), .out_4(\output [0]));
  ETFF etff_2 (.in_1(date[4]), .in_2(not_1_out), .in_3(_0), .out_4(\output [4]));
  not not_1 (not_1_out, and_1_out);
  ETFF etff_3 (.in_1(date[1]), .in_2(not_1_out), .in_3(_0), .out_4(\output [1]));
  ETFF etff_4 (.in_1(date[5]), .in_2(not_1_out), .in_3(_0), .out_4(\output [5]));
  ETFF etff_5 (.in_1(date[2]), .in_2(not_1_out), .in_3(_0), .out_4(\output [2]));
  ETFF etff_6 (.in_1(date[6]), .in_2(not_1_out), .in_3(_0), .out_4(\output [6]));
  ETFF etff_7 (.in_1(date[3]), .in_2(not_1_out), .in_3(_0), .out_4(\output [3]));
  ETFF etff_8 (.in_1(date[7]), .in_2(not_1_out), .in_3(_0), .out_4(\output [7]));
endmodule
