// Logisim project Latch.circ as structural Verilog
module SR_Latch (
  input  set,
  input  reset,
  output out_3
);

  wire nor_1_out;

  nor nor_1 (nor_1_out, set, out_3);
  nor nor_2 (out_3, nor_1_out, reset);
endmodule

module DE_Latch (
  input  data,
  input  enable,
  output out_3
);

  wire and_1_out, and_2_out, nor_1_out, not_1_out;

  not not_1 (not_1_out, data);
  and and_1 (and_1_out, data, enable);
  and and_2 (and_2_out, enable, not_1_out);
  nor nor_1 (nor_1_out, and_1_out, out_3);
  nor nor_2 (out_3, nor_1_out, and_2_out);
endmodule
